// Logisim project hw4.circ as structural Verilog
module RegisterFile (
  input  [15:0] WriteData,
  input  clk,
  input  [2:0] WriteReg,
  input  [2:0] ReadReg1,
  input  Preset,
  input  Reset,
  input  RegWriteEnable,
  input  [2:0] ReadReg2,
  output [15:0] _1,
  output [15:0] _2,
  output [15:0] ReadData1,
  output [15:0] _3,
  output [15:0] _4,
  output [15:0] _5,
  output [15:0] _6,
  output [15:0] _7,
  output [15:0] ReadData2
);

  wire and_1_out, and_2_out, and_3_out, and_4_out, and_5_out, and_6_out, and_7_out, decoder_1_out1,
       decoder_1_out2, decoder_1_out3, decoder_1_out4, decoder_1_out5, decoder_1_out6, decoder_1_out7,
       decoder_2_out0, decoder_2_out1, decoder_2_out2, decoder_2_out3, decoder_2_out4, decoder_2_out5,
       decoder_2_out6, decoder_2_out7, decoder_3_out0, decoder_3_out1, decoder_3_out2, decoder_3_out3,
       decoder_3_out4, decoder_3_out5, decoder_3_out6, decoder_3_out7;
  wire [15:0] n16_bit_register_1_out;

  Decoder #(.select(3), .enable("false")) decoder_1 (
    .out1(decoder_1_out1), .out2(decoder_1_out2), .out3(decoder_1_out3), .out4(decoder_1_out4),
    .out5(decoder_1_out5), .out6(decoder_1_out6), .out7(decoder_1_out7), .sel(WriteReg));  // open: out0
  _16_bit_register u_16_bit_register_1 (
    .In({16{1'b0}}), .Out(n16_bit_register_1_out), .Preset(Preset), .Enable(RegWriteEnable), .Reset(Reset),
    .clk(clk));
  _16_bit_register u_16_bit_register_2 (
    .In(WriteData), .Out(_1), .Preset(Preset), .Enable(and_1_out), .Reset(Reset), .clk(clk));
  and and_1 (and_1_out, decoder_1_out1, RegWriteEnable);
  _16_bit_register u_16_bit_register_3 (
    .In(WriteData), .Out(_2), .Preset(Preset), .Enable(and_2_out), .Reset(Reset), .clk(clk));
  and and_2 (and_2_out, decoder_1_out2, RegWriteEnable);
  _16_bit_register u_16_bit_register_4 (
    .In(WriteData), .Out(_3), .Preset(Preset), .Enable(and_3_out), .Reset(Reset), .clk(clk));
  and and_3 (and_3_out, decoder_1_out3, RegWriteEnable);
  _16_bit_register u_16_bit_register_5 (
    .In(WriteData), .Out(_4), .Preset(Preset), .Enable(and_4_out), .Reset(Reset), .clk(clk));
  and and_4 (and_4_out, decoder_1_out4, RegWriteEnable);
  _16_bit_register u_16_bit_register_6 (
    .In(WriteData), .Out(_5), .Preset(Preset), .Enable(and_5_out), .Reset(Reset), .clk(clk));
  and and_5 (and_5_out, decoder_1_out5, RegWriteEnable);
  _16_bit_register u_16_bit_register_7 (
    .In(WriteData), .Out(_6), .Preset(Preset), .Enable(and_6_out), .Reset(Reset), .clk(clk));
  and and_6 (and_6_out, decoder_1_out6, RegWriteEnable);
  _16_bit_register u_16_bit_register_8 (
    .In(WriteData), .Out(_7), .Preset(Preset), .Enable(and_7_out), .Reset(Reset), .clk(clk));
  and and_7 (and_7_out, decoder_1_out7, RegWriteEnable);
  // Probe on n16_bit_register_1_out
  assign ReadData2 = decoder_2_out0 ? n16_bit_register_1_out : 16'bz;  // Controlled_Buffer controlled_buffer_1
  // Probe on _1
  assign ReadData2 = decoder_2_out1 ? _1 : 16'bz;  // Controlled_Buffer controlled_buffer_2
  // Probe on _2
  assign ReadData2 = decoder_2_out2 ? _2 : 16'bz;  // Controlled_Buffer controlled_buffer_3
  assign ReadData2 = decoder_2_out3 ? _3 : 16'bz;  // Controlled_Buffer controlled_buffer_4
  assign ReadData2 = decoder_2_out4 ? _4 : 16'bz;  // Controlled_Buffer controlled_buffer_5
  Decoder #(.select(3), .enable("false")) decoder_2 (
    .out0(decoder_2_out0), .out1(decoder_2_out1), .out2(decoder_2_out2), .out3(decoder_2_out3),
    .out4(decoder_2_out4), .out5(decoder_2_out5), .out6(decoder_2_out6), .out7(decoder_2_out7), .sel(ReadReg2));
  // Probe on _3
  // Probe on _4
  // Probe on _5
  assign ReadData2 = decoder_2_out5 ? _5 : 16'bz;  // Controlled_Buffer controlled_buffer_6
  // Probe on _6
  assign ReadData2 = decoder_2_out6 ? _6 : 16'bz;  // Controlled_Buffer controlled_buffer_7
  assign ReadData2 = decoder_2_out7 ? _7 : 16'bz;  // Controlled_Buffer controlled_buffer_8
  // Probe on _7
  assign ReadData1 = decoder_3_out1 ? _1 : 16'bz;  // Controlled_Buffer controlled_buffer_9
  assign ReadData1 = decoder_3_out2 ? _2 : 16'bz;  // Controlled_Buffer controlled_buffer_10
  assign ReadData1 = decoder_3_out3 ? _3 : 16'bz;  // Controlled_Buffer controlled_buffer_11
  assign ReadData1 = decoder_3_out4 ? _4 : 16'bz;  // Controlled_Buffer controlled_buffer_12
  assign ReadData1 = decoder_3_out5 ? _5 : 16'bz;  // Controlled_Buffer controlled_buffer_13
  assign ReadData1 = decoder_3_out6 ? _6 : 16'bz;  // Controlled_Buffer controlled_buffer_14
  assign ReadData1 = decoder_3_out7 ? _7 : 16'bz;  // Controlled_Buffer controlled_buffer_15
  assign ReadData1 = decoder_3_out0 ? n16_bit_register_1_out : 16'bz;  // Controlled_Buffer controlled_buffer_16
  Decoder #(.select(3), .enable("false")) decoder_3 (
    .out0(decoder_3_out0), .out1(decoder_3_out1), .out2(decoder_3_out2), .out3(decoder_3_out3),
    .out4(decoder_3_out4), .out5(decoder_3_out5), .out6(decoder_3_out6), .out7(decoder_3_out7), .sel(ReadReg1));
endmodule

module _16_bit_register (
  input  [15:0] In,
  input  clk,
  input  Preset,
  input  Enable,
  input  Reset,
  output [15:0] Out
);

  D_Flip_Flop #(.trigger("falling")) d_ff_1 (
    .clk(clk), .D(In[0]), .Q(Out[0]), .preset(Preset), .en(Enable), .reset(Reset));  // open: Qn
  D_Flip_Flop #(.trigger("falling")) d_ff_2 (
    .clk(clk), .D(In[1]), .Q(Out[1]), .preset(Preset), .en(Enable), .reset(Reset));  // open: Qn
  D_Flip_Flop #(.trigger("falling")) d_ff_3 (
    .clk(clk), .D(In[2]), .Q(Out[2]), .preset(Preset), .en(Enable), .reset(Reset));  // open: Qn
  D_Flip_Flop #(.trigger("falling")) d_ff_4 (
    .clk(clk), .D(In[3]), .Q(Out[3]), .preset(Preset), .en(Enable), .reset(Reset));  // open: Qn
  D_Flip_Flop #(.trigger("falling")) d_ff_5 (
    .clk(clk), .D(In[4]), .Q(Out[4]), .preset(Preset), .en(Enable), .reset(Reset));  // open: Qn
  D_Flip_Flop #(.trigger("falling")) d_ff_6 (
    .clk(clk), .D(In[5]), .Q(Out[5]), .preset(Preset), .en(Enable), .reset(Reset));  // open: Qn
  D_Flip_Flop #(.trigger("falling")) d_ff_7 (
    .clk(clk), .D(In[6]), .Q(Out[6]), .preset(Preset), .en(Enable), .reset(Reset));  // open: Qn
  D_Flip_Flop #(.trigger("falling")) d_ff_8 (
    .clk(clk), .D(In[7]), .Q(Out[7]), .preset(Preset), .en(Enable), .reset(Reset));  // open: Qn
  D_Flip_Flop #(.trigger("falling")) d_ff_9 (
    .clk(clk), .D(In[8]), .Q(Out[8]), .preset(Preset), .en(Enable), .reset(Reset));  // open: Qn
  D_Flip_Flop #(.trigger("falling")) d_ff_10 (
    .clk(clk), .D(In[9]), .Q(Out[9]), .preset(Preset), .en(Enable), .reset(Reset));  // open: Qn
  D_Flip_Flop #(.trigger("falling")) d_ff_11 (
    .clk(clk), .D(In[10]), .Q(Out[10]), .preset(Preset), .en(Enable), .reset(Reset));  // open: Qn
  D_Flip_Flop #(.trigger("falling")) d_ff_12 (
    .clk(clk), .D(In[11]), .Q(Out[11]), .preset(Preset), .en(Enable), .reset(Reset));  // open: Qn
  D_Flip_Flop #(.trigger("falling")) d_ff_13 (
    .clk(clk), .D(In[12]), .Q(Out[12]), .preset(Preset), .en(Enable), .reset(Reset));  // open: Qn
  D_Flip_Flop #(.trigger("falling")) d_ff_14 (
    .clk(clk), .D(In[13]), .Q(Out[13]), .preset(Preset), .en(Enable), .reset(Reset));  // open: Qn
  D_Flip_Flop #(.trigger("falling")) d_ff_15 (
    .clk(clk), .D(In[14]), .Q(Out[14]), .preset(Preset), .en(Enable), .reset(Reset));  // open: Qn
  D_Flip_Flop #(.trigger("falling")) d_ff_16 (
    .clk(clk), .D(In[15]), .Q(Out[15]), .preset(Preset), .en(Enable), .reset(Reset));  // open: Qn
endmodule

module _1_bit_adder (
  input  Cin,
  input  A,
  input  B,
  output Sum,
  output Cout
);

  wire and_1_out, and_2_out, xor_1_out;

  and and_1 (and_1_out, B, A);
  xor xor_1 (xor_1_out, A, B);
  or or_1 (Cout, and_1_out, and_2_out);
  and and_2 (and_2_out, xor_1_out, Cin);
  xor xor_2 (Sum, Cin, xor_1_out);
endmodule

module _16_bit_adder (
  input  sub,
  input  [15:0] B,
  input  [15:0] A,
  output [15:0] result,
  output ovf
);

  wire n1_bit_adder_1_cout, n1_bit_adder_2_cout, n1_bit_adder_3_cout, n1_bit_adder_4_cout,
       n1_bit_adder_5_cout, n1_bit_adder_6_cout, n1_bit_adder_7_cout, n1_bit_adder_8_cout,
       n1_bit_adder_9_cout, n1_bit_adder_10_cout, n1_bit_adder_11_cout, n1_bit_adder_12_cout,
       n1_bit_adder_13_cout, n1_bit_adder_14_cout, n1_bit_adder_15_cout, n1_bit_adder_16_cout, xor_2_out,
       xor_3_out, xor_4_out, xor_5_out, xor_6_out, xor_7_out, xor_8_out, xor_9_out, xor_10_out, xor_11_out,
       xor_12_out, xor_13_out, xor_14_out, xor_15_out, xor_16_out, xor_17_out;

  xor xor_1 (ovf, n1_bit_adder_1_cout, n1_bit_adder_2_cout);
  _1_bit_adder u_1_bit_adder_1 (
    .A(A[15]), .B(xor_2_out), .Sum(result[15]), .Cin(n1_bit_adder_2_cout), .Cout(n1_bit_adder_1_cout));
  xor xor_2 (xor_2_out, sub, B[15]);
  _1_bit_adder u_1_bit_adder_2 (
    .A(A[14]), .B(xor_3_out), .Sum(result[14]), .Cin(n1_bit_adder_3_cout), .Cout(n1_bit_adder_2_cout));
  xor xor_3 (xor_3_out, sub, B[14]);
  _1_bit_adder u_1_bit_adder_3 (
    .A(A[13]), .B(xor_5_out), .Sum(result[13]), .Cin(n1_bit_adder_4_cout), .Cout(n1_bit_adder_3_cout));
  _1_bit_adder u_1_bit_adder_4 (
    .A(A[12]), .B(xor_4_out), .Sum(result[12]), .Cin(n1_bit_adder_5_cout), .Cout(n1_bit_adder_4_cout));
  xor xor_4 (xor_4_out, sub, B[12]);
  xor xor_5 (xor_5_out, sub, B[13]);
  _1_bit_adder u_1_bit_adder_5 (
    .A(A[11]), .B(xor_6_out), .Sum(result[11]), .Cin(n1_bit_adder_6_cout), .Cout(n1_bit_adder_5_cout));
  xor xor_6 (xor_6_out, sub, B[11]);
  _1_bit_adder u_1_bit_adder_6 (
    .A(A[10]), .B(xor_7_out), .Sum(result[10]), .Cin(n1_bit_adder_8_cout), .Cout(n1_bit_adder_6_cout));
  xor xor_7 (xor_7_out, sub, B[10]);
  _1_bit_adder u_1_bit_adder_7 (
    .A(A[8]), .B(xor_8_out), .Sum(result[8]), .Cin(n1_bit_adder_9_cout), .Cout(n1_bit_adder_7_cout));
  _1_bit_adder u_1_bit_adder_8 (
    .A(A[9]), .B(xor_9_out), .Sum(result[9]), .Cin(n1_bit_adder_7_cout), .Cout(n1_bit_adder_8_cout));
  xor xor_8 (xor_8_out, sub, B[8]);
  xor xor_9 (xor_9_out, sub, B[9]);
  _1_bit_adder u_1_bit_adder_9 (
    .A(A[7]), .B(xor_10_out), .Sum(result[7]), .Cin(n1_bit_adder_10_cout), .Cout(n1_bit_adder_9_cout));
  xor xor_10 (xor_10_out, sub, B[7]);
  _1_bit_adder u_1_bit_adder_10 (
    .A(A[6]), .B(xor_11_out), .Sum(result[6]), .Cin(n1_bit_adder_11_cout), .Cout(n1_bit_adder_10_cout));
  xor xor_11 (xor_11_out, sub, B[6]);
  _1_bit_adder u_1_bit_adder_11 (
    .A(A[5]), .B(xor_13_out), .Sum(result[5]), .Cin(n1_bit_adder_12_cout), .Cout(n1_bit_adder_11_cout));
  _1_bit_adder u_1_bit_adder_12 (
    .A(A[4]), .B(xor_12_out), .Sum(result[4]), .Cin(n1_bit_adder_13_cout), .Cout(n1_bit_adder_12_cout));
  xor xor_12 (xor_12_out, sub, B[4]);
  xor xor_13 (xor_13_out, sub, B[5]);
  _1_bit_adder u_1_bit_adder_13 (
    .A(A[3]), .B(xor_14_out), .Sum(result[3]), .Cin(n1_bit_adder_14_cout), .Cout(n1_bit_adder_13_cout));
  xor xor_14 (xor_14_out, sub, B[3]);
  _1_bit_adder u_1_bit_adder_14 (
    .A(A[2]), .B(xor_15_out), .Sum(result[2]), .Cin(n1_bit_adder_15_cout), .Cout(n1_bit_adder_14_cout));
  xor xor_15 (xor_15_out, sub, B[2]);
  _1_bit_adder u_1_bit_adder_15 (
    .A(A[1]), .B(xor_17_out), .Sum(result[1]), .Cin(n1_bit_adder_16_cout), .Cout(n1_bit_adder_15_cout));
  _1_bit_adder u_1_bit_adder_16 (.A(A[0]), .B(xor_16_out), .Sum(result[0]), .Cin(sub), .Cout(n1_bit_adder_16_cout));
  xor xor_16 (xor_16_out, sub, B[0]);
  xor xor_17 (xor_17_out, sub, B[1]);
endmodule

module CPU (
  input  [15:0] From_L2,
  input  Reset,
  output [15:0] To_L2_cache
);

  wire all_zero_1_out_2, and_1_out, and_2_out, and_3_out, and_4_out, clock_1_out, controlled_buffer_11_out,
       instruction_decode_1_blt, instruction_decode_1_bne, instruction_decode_1_iins,
       instruction_decode_1_input, instruction_decode_1_jal, instruction_decode_1_jr,
       instruction_decode_1_jumpins, instruction_decode_1_lw, instruction_decode_1_output,
       instruction_decode_1_rtdest, instruction_decode_1_sw, n16btosignbit_1_neg, not_1_out, not_2_out,
       not_3_out, not_4_out, not_5_out, not_6_out, not_7_out, not_8_out, not_9_out, not_10_out, not_11_out,
       or_1_out, or_3_out;
  wire [2:0] controlled_buffer_8_out, instruction_decode_1_aluop, instruction_decode_1_rd,
       instruction_decode_1_rs, instruction_decode_1_rt, instruction_decode_1_shamt, multiplexer_1_out;
  wire [5:0] instruction_decode_1_imm;
  wire [6:0] controlled_buffer_3_out, keyboard_1_data, n16bto7b_truncator_1_out, pipef_1_out_6;
  wire [11:0] instruction_decode_1_add;
  wire [15:0] alu_1_outputdata, controlled_buffer_1_out, controlled_buffer_5_out, controlled_buffer_13_out,
       multiplexer_2_out, multiplexer_3_out, multiplexer_4_out, multiplexer_5_out, multiplexer_6_out,
       n6bto16b_sx_1_out, n7bto16b_ex_1_out, n12bto16b_sx_1_out, n16_bit_adder_1_result,
       n16_bit_adder_2_result, n16_bit_adder_3_result, n16_bit_register_1_out, or_2_out, piped_1_reg1_2,
       piped_1_reg2_2, pipef_1_ins_2, ram_1_data, registerfile_1_readdata1, registerfile_1_readdata2,
       rom_1_data;

  not not_1 (not_1_out, instruction_decode_1_jr);
  assign controlled_buffer_1_out = not_1_out ? multiplexer_5_out : 16'bz;  // Controlled_Buffer controlled_buffer_1
  assign controlled_buffer_1_out = instruction_decode_1_jr ? piped_1_reg1_2 : 16'bz;  // Controlled_Buffer controlled_buffer_2
  Clock clock_1 (.out(clock_1_out));
  _16_bit_register u_16_bit_register_1 (
    .In(controlled_buffer_1_out), .Out(n16_bit_register_1_out), .Enable(1'b1), .Reset(Reset),
    .clk(clock_1_out));  // open: Preset
  assign controlled_buffer_3_out = not_2_out ? {7{1'b0}} : 7'bz;  // Controlled_Buffer controlled_buffer_3
  not not_2 (not_2_out, instruction_decode_1_output);
  _16_bit_adder u_16_bit_adder_1 (
    .result(n16_bit_adder_1_result), .sub(1'b0), .A(16'h1), .B(n16_bit_register_1_out));  // open: ovf
  _16bto7b_Truncator u_16bto7b_truncator_1 (.Out(n16bto7b_truncator_1_out), .In(piped_1_reg1_2));
  assign controlled_buffer_3_out = instruction_decode_1_output ? n16bto7b_truncator_1_out : 7'bz;  // Controlled_Buffer controlled_buffer_4
  ROM #(.addrWidth(16), .dataWidth(16)) rom_1 (.addr(n16_bit_register_1_out), .data(rom_1_data));  // open: sel
  PipeF pipef_1 (
    .Ins(rom_1_data), .Clk(clock_1_out), .in_3(keyboard_1_data), .Ins_2(pipef_1_ins_2),
    .out_6(pipef_1_out_6), .Reset(Reset));
  TTY #(.rows(13), .cols(80), .trigger("falling")) tty_1 (
    .data(controlled_buffer_3_out), .clk(clock_1_out), .clr(Reset));  // open: we
  _7bto16b_EX u_7bto16b_ex_1 (.In(pipef_1_out_6), .Out(n7bto16b_ex_1_out));
  Keyboard #(.trigger("falling")) keyboard_1 (
    .clk(clock_1_out), .re(instruction_decode_1_input), .data(keyboard_1_data));  // open: clr, avail
  assign controlled_buffer_5_out = instruction_decode_1_jal ? n16_bit_adder_1_result : 16'bz;  // Controlled_Buffer controlled_buffer_5
  not not_3 (not_3_out, instruction_decode_1_input);
  assign controlled_buffer_5_out = not_3_out ? multiplexer_6_out : 16'bz;  // Controlled_Buffer controlled_buffer_6
  assign controlled_buffer_5_out = instruction_decode_1_input ? n7bto16b_ex_1_out : 16'bz;  // Controlled_Buffer controlled_buffer_7
  assign controlled_buffer_8_out = and_1_out ? multiplexer_1_out : 3'bz;  // Controlled_Buffer controlled_buffer_8
  Multiplexer #(.width(3), .enable("false")) multiplexer_1 (
    .in0(instruction_decode_1_rd), .in1(instruction_decode_1_rt), .out(multiplexer_1_out),
    .sel(instruction_decode_1_rtdest));
  assign controlled_buffer_8_out = instruction_decode_1_bne ? 3'b000 : 3'bz;  // Controlled_Buffer controlled_buffer_9
  assign controlled_buffer_8_out = instruction_decode_1_jal ? 3'b111 : 3'bz;  // Controlled_Buffer controlled_buffer_10
  and and_1 (and_1_out, not_6_out, not_5_out, not_4_out);
  not not_4 (not_4_out, instruction_decode_1_jal);
  not not_5 (not_5_out, instruction_decode_1_jumpins);
  not not_6 (not_6_out, instruction_decode_1_bne);
  Instruction_Decode instruction_decode_1 (
    .ALUOp(instruction_decode_1_aluop), .InstructionIN(pipef_1_ins_2), .Rs(instruction_decode_1_rs),
    .Rt(instruction_decode_1_rt), .Rd(instruction_decode_1_rd), .Shamt(instruction_decode_1_shamt),
    .Imm(instruction_decode_1_imm), .Add(instruction_decode_1_add), .JumpIns(instruction_decode_1_jumpins),
    .IIns(instruction_decode_1_iins), .bne(instruction_decode_1_bne), .blt(instruction_decode_1_blt),
    .RtDest(instruction_decode_1_rtdest), .lw(instruction_decode_1_lw), .Output(instruction_decode_1_output),
    .Input(instruction_decode_1_input), .sw(instruction_decode_1_sw), .jr(instruction_decode_1_jr),
    .jal(instruction_decode_1_jal));  // open: RIns
  RegisterFile registerfile_1 (
    .WriteData(controlled_buffer_5_out), .WriteReg(controlled_buffer_8_out),
    .ReadData1(registerfile_1_readdata1), .ReadData2(registerfile_1_readdata2),
    .ReadReg2(instruction_decode_1_rt), .clk(clock_1_out), .Reset(Reset),
    .RegWriteEnable(controlled_buffer_11_out), .ReadReg1(instruction_decode_1_rs));  // open: Preset, _2, _1, _4, _5, _6, _7, _3
  PipeD piped_1 (
    .Clk(clock_1_out), .Reg1(registerfile_1_readdata1), .Reg2(registerfile_1_readdata2), .Ins(pipef_1_ins_2),
    .Reg1_2(piped_1_reg1_2), .Reg2_2(piped_1_reg2_2), .Reset(Reset));  // open: Ins_2
  assign controlled_buffer_11_out = not_7_out ? 1'b1 : 1'bz;  // Controlled_Buffer controlled_buffer_11
  not not_7 (not_7_out, or_1_out);
  assign controlled_buffer_11_out = or_1_out ? 1'b0 : 1'bz;  // Controlled_Buffer controlled_buffer_12
  or or_1 (or_1_out, instruction_decode_1_blt, instruction_decode_1_bne);
  _16_bit_adder u_16_bit_adder_2 (
    .result(n16_bit_adder_2_result), .sub(1'b0), .A(n16_bit_adder_1_result), .B(n6bto16b_sx_1_out));  // open: ovf
  Multiplexer #(.width(16), .enable("false")) multiplexer_2 (
    .in0(piped_1_reg2_2), .in1(n6bto16b_sx_1_out), .out(multiplexer_2_out), .sel(and_2_out));
  and and_2 (and_2_out, not_11_out, instruction_decode_1_iins, not_9_out);
  _6bto16b_SX u_6bto16b_sx_1 (.In(instruction_decode_1_imm), .Out(n6bto16b_sx_1_out));
  assign or_2_out = {16{1'b0}} | alu_1_outputdata;  // OR_Gate or_2, 16 bits wide
  ALU alu_1 (
    .InputData1(piped_1_reg1_2), .InputData2(multiplexer_2_out), .Shamt(instruction_decode_1_shamt),
    .OutputData(alu_1_outputdata), .OpType(instruction_decode_1_aluop));
  All_Zero all_zero_1 (.in_1(or_2_out), .out_2(all_zero_1_out_2));
  assign controlled_buffer_13_out = instruction_decode_1_sw ? piped_1_reg2_2 : 16'bz;  // Controlled_Buffer controlled_buffer_13
  and and_3 (and_3_out, instruction_decode_1_bne, not_8_out);
  not not_8 (not_8_out, all_zero_1_out_2);
  _16_bit_adder u_16_bit_adder_3 (
    .result(n16_bit_adder_3_result), .sub(1'b0), .A(piped_1_reg1_2), .B(n6bto16b_sx_1_out));  // open: ovf
  not not_9 (not_9_out, instruction_decode_1_blt);
  Multiplexer #(.width(16), .enable("false")) multiplexer_3 (
    .in0(n16_bit_adder_1_result), .in1(n16_bit_adder_2_result), .out(multiplexer_3_out), .sel(or_3_out));
  or or_3 (or_3_out, and_3_out, and_4_out);
  and and_4 (and_4_out, n16btosignbit_1_neg, instruction_decode_1_blt);
  Multiplexer #(.width(16), .enable("false")) multiplexer_4 (
    .in0(n6bto16b_sx_1_out), .in1(n12bto16b_sx_1_out), .out(multiplexer_4_out),
    .sel(instruction_decode_1_jumpins));
  _16btosignbit u_16btosignbit_1 (.IN(alu_1_outputdata), .NEG(n16btosignbit_1_neg));
  _12bto16b_SX u_12bto16b_sx_1 (.In(instruction_decode_1_add), .Out(n12bto16b_sx_1_out));
  not not_10 (not_10_out, clock_1_out);
  not not_11 (not_11_out, instruction_decode_1_bne);
  Multiplexer #(.width(16), .enable("false")) multiplexer_5 (
    .in0(multiplexer_3_out), .in1(multiplexer_4_out), .out(multiplexer_5_out),
    .sel(instruction_decode_1_jumpins));
  RAM #(.addrWidth(16), .dataWidth(16), .bus("separate")) ram_1 (
    .addr(n16_bit_adder_3_result), .din(controlled_buffer_13_out), .data(ram_1_data),
    .str(instruction_decode_1_sw), .clk(not_10_out), .ld(instruction_decode_1_lw));  // open: sel, clr
  assign controlled_buffer_13_out = instruction_decode_1_lw ? ram_1_data : 16'bz;  // Controlled_Buffer controlled_buffer_14
  Multiplexer #(.width(16), .enable("false")) multiplexer_6 (
    .in0(alu_1_outputdata), .in1(ram_1_data), .out(multiplexer_6_out), .sel(instruction_decode_1_lw));

  // Notes on the sheet:
  //   contents of rom_1 (hex, n*v repeats v):
  //   1100 1903 e040 12a0 f400 193f 983b 91ff 1fc1 91ff
endmodule

module ALU (
  input  [15:0] InputData1,
  input  [15:0] InputData2,
  input  [2:0] Shamt,
  input  [2:0] OpType,
  output [15:0] OutputData
);

  wire decoder_1_out0, decoder_1_out1, decoder_1_out2, decoder_1_out3, decoder_1_out4, decoder_1_out5,
       decoder_1_out6, or_1_out;
  wire [15:0] _0000_0010_result, _0011_out, _0100_out, left_bit_shifter_1_out, right_bit_shifter_1_out;

  _16_bit_adder _0000_0010 (
    .result(_0000_0010_result), .sub(decoder_1_out2), .A(InputData1), .B(InputData2));  // open: ovf
  assign _0011_out = ~InputData1;  // NOT_Gate _0011, 16 bits wide
  assign _0100_out = InputData1 ^ InputData2;  // XOR_Gate _0100, 16 bits wide
  Left_Bit_Shifter left_bit_shifter_1 (.IN(InputData1), .OUT(left_bit_shifter_1_out), .Shamt(Shamt));
  Right_Bit_Shifter right_bit_shifter_1 (.IN(InputData1), .OUT(right_bit_shifter_1_out), .Shamt(Shamt));
  assign OutputData = or_1_out ? _0000_0010_result : 16'bz;  // Controlled_Buffer controlled_buffer_1
  assign OutputData = decoder_1_out3 ? _0011_out : 16'bz;  // Controlled_Buffer controlled_buffer_2
  assign OutputData = decoder_1_out4 ? _0100_out : 16'bz;  // Controlled_Buffer controlled_buffer_3
  assign OutputData = decoder_1_out5 ? left_bit_shifter_1_out : 16'bz;  // Controlled_Buffer controlled_buffer_4
  assign OutputData = decoder_1_out6 ? right_bit_shifter_1_out : 16'bz;  // Controlled_Buffer controlled_buffer_5
  or or_1 (or_1_out, decoder_1_out0, decoder_1_out1, decoder_1_out2);
  Decoder #(.select(3), .enable("false")) decoder_1 (
    .out0(decoder_1_out0), .out1(decoder_1_out1), .out2(decoder_1_out2), .out3(decoder_1_out3),
    .out4(decoder_1_out4), .out5(decoder_1_out5), .out6(decoder_1_out6), .sel(OpType));  // open: out7

  // Notes on the sheet:
  //   0101-0110
endmodule

module Instruction_Decode (
  input  [15:0] InstructionIN,
  output jr,
  output jal,
  output sw,
  output JumpIns,
  output lw,
  output Output,
  output [2:0] ALUOp,
  output Input,
  output IIns,
  output RIns,
  output [11:0] Add,
  output RtDest,
  output [5:0] Imm,
  output [2:0] Rs,
  output [2:0] Rt,
  output bne,
  output blt,
  output [2:0] Shamt,
  output [2:0] Rd
);

  wire and_4_out, and_6_out, and_8_out, and_11_out, and_12_out, and_13_out, and_14_out, and_15_out,
       and_16_out, and_19_out, and_20_out, and_21_out, and_22_out, and_23_out, not_1_out, not_2_out,
       not_3_out, not_4_out, not_5_out, not_6_out, not_7_out, not_8_out, not_9_out, not_10_out, not_11_out,
       not_12_out, not_13_out, not_14_out, not_15_out, not_16_out, not_17_out, not_18_out, not_19_out,
       not_20_out, not_21_out, not_22_out, or_2_out, or_3_out, or_4_out, xnor_1_out, xor_1_out;

  and and_1 (sw, not_2_out, not_3_out, not_4_out, InstructionIN[15]);
  and and_2 (Output, InstructionIN[15], InstructionIN[14], InstructionIN[13], InstructionIN[12]);
  and and_3 (Input, InstructionIN[15], InstructionIN[14], InstructionIN[13], not_1_out);
  not not_1 (not_1_out, InstructionIN[12]);
  or or_1 (RtDest, Input, and_4_out);
  and and_4 (and_4_out, and_6_out, xnor_1_out);
  not not_2 (not_2_out, InstructionIN[14]);
  not not_3 (not_3_out, InstructionIN[13]);
  not not_4 (not_4_out, InstructionIN[12]);
  and and_5 (lw, InstructionIN[13], InstructionIN[12], InstructionIN[14], not_5_out);
  not not_5 (not_5_out, InstructionIN[15]);
  and and_6 (and_6_out, InstructionIN[12], not_6_out);
  not not_6 (not_6_out, InstructionIN[15]);
  xnor xnor_1 (xnor_1_out, InstructionIN[13], InstructionIN[14]);
  and and_7 (jr, InstructionIN[15], InstructionIN[14], not_7_out, not_8_out);
  not not_7 (not_7_out, InstructionIN[13]);
  not not_8 (not_8_out, InstructionIN[12]);
  not not_9 (not_9_out, InstructionIN[13]);
  and and_8 (and_8_out, not_9_out, InstructionIN[12]);
  and and_9 (bne, and_8_out, and_11_out);
  and and_10 (jal, InstructionIN[14], not_10_out, JumpIns);
  not not_10 (not_10_out, InstructionIN[13]);
  assign ALUOp = not_11_out ? InstructionIN[14:12] : 3'bz;  // Controlled_Buffer controlled_buffer_1
  not not_11 (not_11_out, InstructionIN[15]);
  not not_12 (not_12_out, InstructionIN[14]);
  and and_11 (and_11_out, not_12_out, InstructionIN[15]);
  and and_12 (and_12_out, InstructionIN[12], InstructionIN[15]);
  xor xor_1 (xor_1_out, InstructionIN[14], InstructionIN[13]);
  assign ALUOp = and_13_out ? 3'b111 : 3'bz;  // Controlled_Buffer controlled_buffer_2
  and and_13 (and_13_out, not_14_out, InstructionIN[15], not_13_out);
  not not_13 (not_13_out, blt);
  not not_14 (not_14_out, bne);
  not not_15 (not_15_out, InstructionIN[12]);
  and and_14 (and_14_out, not_15_out, InstructionIN[13]);
  and and_15 (and_15_out, InstructionIN[15], not_16_out);
  not not_16 (not_16_out, InstructionIN[14]);
  not not_17 (not_17_out, InstructionIN[12]);
  and and_16 (and_16_out, InstructionIN[13], not_17_out);
  and and_17 (blt, and_11_out, and_16_out);
  and and_18 (JumpIns, and_12_out, xor_1_out);
  not not_18 (not_18_out, xor_1_out);
  or or_2 (or_2_out, InstructionIN[15], InstructionIN[12]);
  and and_19 (and_19_out, and_14_out, and_15_out);
  not not_19 (not_19_out, InstructionIN[14]);
  and and_20 (and_20_out, not_19_out, not_20_out);
  not not_20 (not_20_out, InstructionIN[13]);
  or or_3 (or_3_out, InstructionIN[12], InstructionIN[15]);
  and and_21 (and_21_out, not_18_out, and_12_out);
  and and_22 (and_22_out, InstructionIN[13], InstructionIN[14], or_2_out);
  and and_23 (and_23_out, and_20_out, or_3_out);
  assign ALUOp = or_4_out ? 3'b010 : 3'bz;  // Controlled_Buffer controlled_buffer_3
  or or_4 (or_4_out, bne, blt);
  or or_5 (IIns, and_21_out, and_22_out, and_19_out, and_23_out);
  not not_21 (not_21_out, JumpIns);
  not not_22 (not_22_out, IIns);
  and and_24 (RIns, not_21_out, not_22_out);

  assign Add = InstructionIN[11:0];
  assign Imm = InstructionIN[5:0];
  assign Rd = InstructionIN[5:3];
  assign Rs = InstructionIN[11:9];
  assign Rt = InstructionIN[8:6];
  assign Shamt = InstructionIN[2:0];

  // Other names for the same wires on the sheet: NonOp[11:0] = {InstructionIN[0], InstructionIN[1], InstructionIN[2], InstructionIN[3], InstructionIN[4], InstructionIN[5], InstructionIN[6], InstructionIN[7], InstructionIN[8], InstructionIN[9], InstructionIN[10], InstructionIN[11]}

  // Notes on the sheet:
  //   OPcode
endmodule

module _6bto16b_SX (
  input  [5:0] In,
  output [15:0] Out
);


  assign Out = {{11{In[5]}}, In[4:0]};
endmodule

module Left_Bit_Shifter (
  input  [15:0] IN,
  input  [2:0] Shamt,
  output [15:0] OUT
);

  wire multiplexer_1_out, multiplexer_2_out, multiplexer_3_out, multiplexer_4_out, multiplexer_5_out,
       multiplexer_6_out, multiplexer_7_out, multiplexer_8_out, multiplexer_9_out, multiplexer_10_out,
       multiplexer_11_out, multiplexer_12_out, multiplexer_13_out, multiplexer_14_out, multiplexer_15_out,
       multiplexer_16_out, multiplexer_17_out, multiplexer_18_out, multiplexer_19_out, multiplexer_20_out,
       multiplexer_21_out, multiplexer_23_out, multiplexer_24_out, multiplexer_25_out, multiplexer_26_out,
       multiplexer_29_out, multiplexer_30_out, multiplexer_31_out, multiplexer_34_out, multiplexer_35_out,
       multiplexer_38_out, multiplexer_39_out;

  Multiplexer #(.enable("false")) multiplexer_1 (.in0(IN[0]), .in1(1'b0), .out(multiplexer_1_out), .sel(Shamt[0]));
  Multiplexer #(.enable("false")) multiplexer_2 (.in0(IN[2]), .in1(IN[1]), .out(multiplexer_2_out), .sel(Shamt[0]));
  Multiplexer #(.enable("false")) multiplexer_3 (.in0(IN[1]), .in1(IN[0]), .out(multiplexer_3_out), .sel(Shamt[0]));
  Multiplexer #(.enable("false")) multiplexer_4 (.in0(IN[4]), .in1(IN[3]), .out(multiplexer_4_out), .sel(Shamt[0]));
  Multiplexer #(.enable("false")) multiplexer_5 (.in0(IN[3]), .in1(IN[2]), .out(multiplexer_5_out), .sel(Shamt[0]));
  Multiplexer #(.enable("false")) multiplexer_6 (.in0(IN[6]), .in1(IN[5]), .out(multiplexer_6_out), .sel(Shamt[0]));
  Multiplexer #(.enable("false")) multiplexer_7 (.in0(IN[5]), .in1(IN[4]), .out(multiplexer_7_out), .sel(Shamt[0]));
  Multiplexer #(.enable("false")) multiplexer_8 (
    .in0(multiplexer_3_out), .in1(1'b0), .out(multiplexer_8_out), .sel(Shamt[1]));
  Multiplexer #(.enable("false")) multiplexer_9 (
    .in0(multiplexer_1_out), .in1(1'b0), .out(multiplexer_9_out), .sel(Shamt[1]));
  Multiplexer #(.enable("false")) multiplexer_10 (.in0(IN[8]), .in1(IN[7]), .out(multiplexer_10_out), .sel(Shamt[0]));
  Multiplexer #(.enable("false")) multiplexer_11 (.in0(IN[7]), .in1(IN[6]), .out(multiplexer_11_out), .sel(Shamt[0]));
  Multiplexer #(.enable("false")) multiplexer_12 (
    .in0(multiplexer_5_out), .in1(multiplexer_3_out), .out(multiplexer_12_out), .sel(Shamt[1]));
  Multiplexer #(.enable("false")) multiplexer_13 (
    .in0(multiplexer_2_out), .in1(multiplexer_1_out), .out(multiplexer_13_out), .sel(Shamt[1]));
  Multiplexer #(.enable("false")) multiplexer_14 (.in0(IN[10]), .in1(IN[9]), .out(multiplexer_14_out), .sel(Shamt[0]));
  Multiplexer #(.enable("false")) multiplexer_15 (.in0(IN[9]), .in1(IN[8]), .out(multiplexer_15_out), .sel(Shamt[0]));
  Multiplexer #(.enable("false")) multiplexer_16 (
    .in0(multiplexer_7_out), .in1(multiplexer_5_out), .out(multiplexer_16_out), .sel(Shamt[1]));
  Multiplexer #(.enable("false")) multiplexer_17 (
    .in0(multiplexer_4_out), .in1(multiplexer_2_out), .out(multiplexer_17_out), .sel(Shamt[1]));
  Multiplexer #(.enable("false")) multiplexer_18 (.in0(IN[12]), .in1(IN[11]), .out(multiplexer_18_out), .sel(Shamt[0]));
  Multiplexer #(.enable("false")) multiplexer_19 (.in0(IN[11]), .in1(IN[10]), .out(multiplexer_19_out), .sel(Shamt[0]));
  Multiplexer #(.enable("false")) multiplexer_20 (
    .in0(multiplexer_11_out), .in1(multiplexer_7_out), .out(multiplexer_20_out), .sel(Shamt[1]));
  Multiplexer #(.enable("false")) multiplexer_21 (
    .in0(multiplexer_6_out), .in1(multiplexer_4_out), .out(multiplexer_21_out), .sel(Shamt[1]));
  Multiplexer #(.enable("false")) multiplexer_22 (.in0(multiplexer_9_out), .in1(1'b0), .out(OUT[0]), .sel(Shamt[2]));
  Multiplexer #(.enable("false")) multiplexer_23 (.in0(IN[14]), .in1(IN[13]), .out(multiplexer_23_out), .sel(Shamt[0]));
  Multiplexer #(.enable("false")) multiplexer_24 (.in0(IN[13]), .in1(IN[12]), .out(multiplexer_24_out), .sel(Shamt[0]));
  Multiplexer #(.enable("false")) multiplexer_25 (
    .in0(multiplexer_15_out), .in1(multiplexer_11_out), .out(multiplexer_25_out), .sel(Shamt[1]));
  Multiplexer #(.enable("false")) multiplexer_26 (
    .in0(multiplexer_10_out), .in1(multiplexer_6_out), .out(multiplexer_26_out), .sel(Shamt[1]));
  Multiplexer #(.enable("false")) multiplexer_27 (.in0(multiplexer_13_out), .in1(1'b0), .out(OUT[2]), .sel(Shamt[2]));
  Multiplexer #(.enable("false")) multiplexer_28 (.in0(multiplexer_8_out), .in1(1'b0), .out(OUT[1]), .sel(Shamt[2]));
  Multiplexer #(.enable("false")) multiplexer_29 (.in0(IN[15]), .in1(IN[14]), .out(multiplexer_29_out), .sel(Shamt[0]));
  Multiplexer #(.enable("false")) multiplexer_30 (
    .in0(multiplexer_19_out), .in1(multiplexer_15_out), .out(multiplexer_30_out), .sel(Shamt[1]));
  Multiplexer #(.enable("false")) multiplexer_31 (
    .in0(multiplexer_14_out), .in1(multiplexer_10_out), .out(multiplexer_31_out), .sel(Shamt[1]));
  Multiplexer #(.enable("false")) multiplexer_32 (
    .in0(multiplexer_17_out), .in1(multiplexer_9_out), .out(OUT[4]), .sel(Shamt[2]));
  Multiplexer #(.enable("false")) multiplexer_33 (.in0(multiplexer_12_out), .in1(1'b0), .out(OUT[3]), .sel(Shamt[2]));
  Multiplexer #(.enable("false")) multiplexer_34 (
    .in0(multiplexer_24_out), .in1(multiplexer_19_out), .out(multiplexer_34_out), .sel(Shamt[1]));
  Multiplexer #(.enable("false")) multiplexer_35 (
    .in0(multiplexer_18_out), .in1(multiplexer_14_out), .out(multiplexer_35_out), .sel(Shamt[1]));
  Multiplexer #(.enable("false")) multiplexer_36 (
    .in0(multiplexer_21_out), .in1(multiplexer_13_out), .out(OUT[6]), .sel(Shamt[2]));
  Multiplexer #(.enable("false")) multiplexer_37 (
    .in0(multiplexer_16_out), .in1(multiplexer_8_out), .out(OUT[5]), .sel(Shamt[2]));
  Multiplexer #(.enable("false")) multiplexer_38 (
    .in0(multiplexer_29_out), .in1(multiplexer_24_out), .out(multiplexer_38_out), .sel(Shamt[1]));
  Multiplexer #(.enable("false")) multiplexer_39 (
    .in0(multiplexer_23_out), .in1(multiplexer_18_out), .out(multiplexer_39_out), .sel(Shamt[1]));
  Multiplexer #(.enable("false")) multiplexer_40 (
    .in0(multiplexer_26_out), .in1(multiplexer_17_out), .out(OUT[8]), .sel(Shamt[2]));
  Multiplexer #(.enable("false")) multiplexer_41 (
    .in0(multiplexer_20_out), .in1(multiplexer_12_out), .out(OUT[7]), .sel(Shamt[2]));
  Multiplexer #(.enable("false")) multiplexer_42 (
    .in0(multiplexer_31_out), .in1(multiplexer_21_out), .out(OUT[10]), .sel(Shamt[2]));
  Multiplexer #(.enable("false")) multiplexer_43 (
    .in0(multiplexer_25_out), .in1(multiplexer_16_out), .out(OUT[9]), .sel(Shamt[2]));
  Multiplexer #(.enable("false")) multiplexer_44 (
    .in0(multiplexer_35_out), .in1(multiplexer_26_out), .out(OUT[12]), .sel(Shamt[2]));
  Multiplexer #(.enable("false")) multiplexer_45 (
    .in0(multiplexer_30_out), .in1(multiplexer_20_out), .out(OUT[11]), .sel(Shamt[2]));
  Multiplexer #(.enable("false")) multiplexer_46 (
    .in0(multiplexer_39_out), .in1(multiplexer_31_out), .out(OUT[14]), .sel(Shamt[2]));
  Multiplexer #(.enable("false")) multiplexer_47 (
    .in0(multiplexer_34_out), .in1(multiplexer_25_out), .out(OUT[13]), .sel(Shamt[2]));
  Multiplexer #(.enable("false")) multiplexer_48 (
    .in0(multiplexer_38_out), .in1(multiplexer_30_out), .out(OUT[15]), .sel(Shamt[2]));
endmodule

module Right_Bit_Shifter (
  input  [15:0] IN,
  input  [2:0] Shamt,
  output [15:0] OUT
);

  wire multiplexer_1_out, multiplexer_2_out, multiplexer_3_out, multiplexer_4_out, multiplexer_5_out,
       multiplexer_6_out, multiplexer_7_out, multiplexer_8_out, multiplexer_9_out, multiplexer_10_out,
       multiplexer_11_out, multiplexer_12_out, multiplexer_13_out, multiplexer_14_out, multiplexer_15_out,
       multiplexer_16_out, multiplexer_17_out, multiplexer_18_out, multiplexer_19_out, multiplexer_20_out,
       multiplexer_21_out, multiplexer_23_out, multiplexer_24_out, multiplexer_25_out, multiplexer_26_out,
       multiplexer_29_out, multiplexer_30_out, multiplexer_31_out, multiplexer_34_out, multiplexer_35_out,
       multiplexer_38_out, multiplexer_39_out;

  Multiplexer #(.enable("false")) multiplexer_1 (.in0(IN[15]), .in1(1'b0), .out(multiplexer_1_out), .sel(Shamt[0]));
  Multiplexer #(.enable("false")) multiplexer_2 (.in0(IN[13]), .in1(IN[14]), .out(multiplexer_2_out), .sel(Shamt[0]));
  Multiplexer #(.enable("false")) multiplexer_3 (.in0(IN[14]), .in1(IN[15]), .out(multiplexer_3_out), .sel(Shamt[0]));
  Multiplexer #(.enable("false")) multiplexer_4 (.in0(IN[11]), .in1(IN[12]), .out(multiplexer_4_out), .sel(Shamt[0]));
  Multiplexer #(.enable("false")) multiplexer_5 (.in0(IN[12]), .in1(IN[13]), .out(multiplexer_5_out), .sel(Shamt[0]));
  Multiplexer #(.enable("false")) multiplexer_6 (.in0(IN[9]), .in1(IN[10]), .out(multiplexer_6_out), .sel(Shamt[0]));
  Multiplexer #(.enable("false")) multiplexer_7 (.in0(IN[10]), .in1(IN[11]), .out(multiplexer_7_out), .sel(Shamt[0]));
  Multiplexer #(.enable("false")) multiplexer_8 (
    .in0(multiplexer_3_out), .in1(1'b0), .out(multiplexer_8_out), .sel(Shamt[1]));
  Multiplexer #(.enable("false")) multiplexer_9 (
    .in0(multiplexer_1_out), .in1(1'b0), .out(multiplexer_9_out), .sel(Shamt[1]));
  Multiplexer #(.enable("false")) multiplexer_10 (.in0(IN[7]), .in1(IN[8]), .out(multiplexer_10_out), .sel(Shamt[0]));
  Multiplexer #(.enable("false")) multiplexer_11 (.in0(IN[8]), .in1(IN[9]), .out(multiplexer_11_out), .sel(Shamt[0]));
  Multiplexer #(.enable("false")) multiplexer_12 (
    .in0(multiplexer_5_out), .in1(multiplexer_3_out), .out(multiplexer_12_out), .sel(Shamt[1]));
  Multiplexer #(.enable("false")) multiplexer_13 (
    .in0(multiplexer_2_out), .in1(multiplexer_1_out), .out(multiplexer_13_out), .sel(Shamt[1]));
  Multiplexer #(.enable("false")) multiplexer_14 (.in0(IN[5]), .in1(IN[6]), .out(multiplexer_14_out), .sel(Shamt[0]));
  Multiplexer #(.enable("false")) multiplexer_15 (.in0(IN[6]), .in1(IN[7]), .out(multiplexer_15_out), .sel(Shamt[0]));
  Multiplexer #(.enable("false")) multiplexer_16 (
    .in0(multiplexer_7_out), .in1(multiplexer_5_out), .out(multiplexer_16_out), .sel(Shamt[1]));
  Multiplexer #(.enable("false")) multiplexer_17 (
    .in0(multiplexer_4_out), .in1(multiplexer_2_out), .out(multiplexer_17_out), .sel(Shamt[1]));
  Multiplexer #(.enable("false")) multiplexer_18 (.in0(IN[3]), .in1(IN[4]), .out(multiplexer_18_out), .sel(Shamt[0]));
  Multiplexer #(.enable("false")) multiplexer_19 (.in0(IN[4]), .in1(IN[5]), .out(multiplexer_19_out), .sel(Shamt[0]));
  Multiplexer #(.enable("false")) multiplexer_20 (
    .in0(multiplexer_11_out), .in1(multiplexer_7_out), .out(multiplexer_20_out), .sel(Shamt[1]));
  Multiplexer #(.enable("false")) multiplexer_21 (
    .in0(multiplexer_6_out), .in1(multiplexer_4_out), .out(multiplexer_21_out), .sel(Shamt[1]));
  Multiplexer #(.enable("false")) multiplexer_22 (.in0(multiplexer_9_out), .in1(1'b0), .out(OUT[15]), .sel(Shamt[2]));
  Multiplexer #(.enable("false")) multiplexer_23 (.in0(IN[1]), .in1(IN[2]), .out(multiplexer_23_out), .sel(Shamt[0]));
  Multiplexer #(.enable("false")) multiplexer_24 (.in0(IN[2]), .in1(IN[3]), .out(multiplexer_24_out), .sel(Shamt[0]));
  Multiplexer #(.enable("false")) multiplexer_25 (
    .in0(multiplexer_15_out), .in1(multiplexer_11_out), .out(multiplexer_25_out), .sel(Shamt[1]));
  Multiplexer #(.enable("false")) multiplexer_26 (
    .in0(multiplexer_10_out), .in1(multiplexer_6_out), .out(multiplexer_26_out), .sel(Shamt[1]));
  Multiplexer #(.enable("false")) multiplexer_27 (.in0(multiplexer_13_out), .in1(1'b0), .out(OUT[13]), .sel(Shamt[2]));
  Multiplexer #(.enable("false")) multiplexer_28 (.in0(multiplexer_8_out), .in1(1'b0), .out(OUT[14]), .sel(Shamt[2]));
  Multiplexer #(.enable("false")) multiplexer_29 (.in0(IN[0]), .in1(IN[1]), .out(multiplexer_29_out), .sel(Shamt[0]));
  Multiplexer #(.enable("false")) multiplexer_30 (
    .in0(multiplexer_19_out), .in1(multiplexer_15_out), .out(multiplexer_30_out), .sel(Shamt[1]));
  Multiplexer #(.enable("false")) multiplexer_31 (
    .in0(multiplexer_14_out), .in1(multiplexer_10_out), .out(multiplexer_31_out), .sel(Shamt[1]));
  Multiplexer #(.enable("false")) multiplexer_32 (
    .in0(multiplexer_17_out), .in1(multiplexer_9_out), .out(OUT[11]), .sel(Shamt[2]));
  Multiplexer #(.enable("false")) multiplexer_33 (.in0(multiplexer_12_out), .in1(1'b0), .out(OUT[12]), .sel(Shamt[2]));
  Multiplexer #(.enable("false")) multiplexer_34 (
    .in0(multiplexer_24_out), .in1(multiplexer_19_out), .out(multiplexer_34_out), .sel(Shamt[1]));
  Multiplexer #(.enable("false")) multiplexer_35 (
    .in0(multiplexer_18_out), .in1(multiplexer_14_out), .out(multiplexer_35_out), .sel(Shamt[1]));
  Multiplexer #(.enable("false")) multiplexer_36 (
    .in0(multiplexer_21_out), .in1(multiplexer_13_out), .out(OUT[9]), .sel(Shamt[2]));
  Multiplexer #(.enable("false")) multiplexer_37 (
    .in0(multiplexer_16_out), .in1(multiplexer_8_out), .out(OUT[10]), .sel(Shamt[2]));
  Multiplexer #(.enable("false")) multiplexer_38 (
    .in0(multiplexer_29_out), .in1(multiplexer_24_out), .out(multiplexer_38_out), .sel(Shamt[1]));
  Multiplexer #(.enable("false")) multiplexer_39 (
    .in0(multiplexer_23_out), .in1(multiplexer_18_out), .out(multiplexer_39_out), .sel(Shamt[1]));
  Multiplexer #(.enable("false")) multiplexer_40 (
    .in0(multiplexer_26_out), .in1(multiplexer_17_out), .out(OUT[7]), .sel(Shamt[2]));
  Multiplexer #(.enable("false")) multiplexer_41 (
    .in0(multiplexer_20_out), .in1(multiplexer_12_out), .out(OUT[8]), .sel(Shamt[2]));
  Multiplexer #(.enable("false")) multiplexer_42 (
    .in0(multiplexer_31_out), .in1(multiplexer_21_out), .out(OUT[5]), .sel(Shamt[2]));
  Multiplexer #(.enable("false")) multiplexer_43 (
    .in0(multiplexer_25_out), .in1(multiplexer_16_out), .out(OUT[6]), .sel(Shamt[2]));
  Multiplexer #(.enable("false")) multiplexer_44 (
    .in0(multiplexer_35_out), .in1(multiplexer_26_out), .out(OUT[3]), .sel(Shamt[2]));
  Multiplexer #(.enable("false")) multiplexer_45 (
    .in0(multiplexer_30_out), .in1(multiplexer_20_out), .out(OUT[4]), .sel(Shamt[2]));
  Multiplexer #(.enable("false")) multiplexer_46 (
    .in0(multiplexer_39_out), .in1(multiplexer_31_out), .out(OUT[1]), .sel(Shamt[2]));
  Multiplexer #(.enable("false")) multiplexer_47 (
    .in0(multiplexer_34_out), .in1(multiplexer_25_out), .out(OUT[2]), .sel(Shamt[2]));
  Multiplexer #(.enable("false")) multiplexer_48 (
    .in0(multiplexer_38_out), .in1(multiplexer_30_out), .out(OUT[0]), .sel(Shamt[2]));
endmodule

module _12bto16b_SX (
  input  [11:0] In,
  output [15:0] Out
);


  assign Out = {{5{In[11]}}, In[10:0]};
endmodule

module All_Zero (
  input  [15:0] in_1,
  output out_2
);

  nor nor_1 (out_2, in_1[0], in_1[1], in_1[2], in_1[3], in_1[4], in_1[5], in_1[6], in_1[7], in_1[8], in_1[9], in_1[10], in_1[11], in_1[12], in_1[13], in_1[14], in_1[15]);
endmodule

module _7bto16b_EX (
  input  [6:0] In,
  output [15:0] Out
);


  assign Out = {{9{1'b0}}, In};
endmodule

module _16bto7b_Truncator (
  input  [15:0] In,
  output [6:0] Out
);


  assign Out = In[6:0];
endmodule

module _16btosignbit (
  input  [15:0] IN,
  output NEG
);


  assign NEG = IN[15];
endmodule

module MultiCore (
  input  Reset
);

  wire clock_1_out;
  wire [15:0] cpu_1_to_l2_cache, cpu_2_to_l2_cache, multiplexer_1_out, ram_1_data;

  Clock clock_1 (.out(clock_1_out));
  CPU cpu_1 (.Reset(Reset), .To_L2_cache(cpu_1_to_l2_cache), .From_L2(ram_1_data));
  CPU cpu_2 (.Reset(Reset), .To_L2_cache(cpu_2_to_l2_cache), .From_L2(ram_1_data));
  Multiplexer #(.width(16), .enable("false")) multiplexer_1 (
    .in0(cpu_1_to_l2_cache), .in1(cpu_2_to_l2_cache), .out(multiplexer_1_out));  // open: sel
  RAM #(.addrWidth(16), .dataWidth(16)) ram_1 (
    .addr(multiplexer_1_out), .data(ram_1_data), .clk(clock_1_out));  // open: sel, ld, clr
endmodule

module PipeF (
  input  [15:0] Ins,
  input  Clk,
  input  [6:0] in_3,
  input  Reset,
  output [15:0] Ins_2,
  output [6:0] out_6
);

  wire [15:0] n7bto16b_ex_1_out, n16_bit_register_2_out;

  _7bto16b_EX u_7bto16b_ex_1 (.In(in_3), .Out(n7bto16b_ex_1_out));
  _16_bit_register u_16_bit_register_1 (
    .In(Ins), .Out(Ins_2), .Enable(1'b1), .Reset(Reset), .clk(Clk));  // open: Preset
  _16_bit_register u_16_bit_register_2 (
    .In(n7bto16b_ex_1_out), .Out(n16_bit_register_2_out), .Enable(1'b1), .Reset(Reset), .clk(Clk));  // open: Preset
  _16bto7b_Truncator u_16bto7b_truncator_1 (.Out(out_6), .In(n16_bit_register_2_out));
endmodule

module PipeD (
  input  Clk,
  input  [15:0] Reg1,
  input  [15:0] Reg2,
  input  [15:0] Ins,
  input  Reset,
  output [15:0] Reg1_2,
  output [15:0] Reg2_2,
  output [15:0] Ins_2
);

  _16_bit_register u_16_bit_register_1 (
    .In(Reg1), .Out(Reg1_2), .Enable(1'b1), .Reset(Reset), .clk(Clk));  // open: Preset
  _16_bit_register u_16_bit_register_2 (
    .In(Reg2), .Out(Reg2_2), .Enable(1'b1), .Reset(Reset), .clk(Clk));  // open: Preset
  _16_bit_register u_16_bit_register_3 (
    .In(Ins), .Out(Ins_2), .Enable(1'b1), .Reset(Reset), .clk(Clk));  // open: Preset
endmodule
